# Fritzing sketch master_schematic (saved by Fritzing 1.0.4)
breadboards: 1

parts:
  HX711 = HX711 Weighing Sensor Module
  S1 = Load Sensor - 50kg [part_number=SEN-10245]
  LoRa_Module1 = Ra-01 - LoRa Module SX1278 [part_number=SX1278]
  LCD1602_I2C = LCD1602-I2C
  S2 = Load Sensor - 50kg [part_number=SEN-10245]
  S3 = Load Sensor - 50kg [part_number=SEN-10245]
  S4 = Load Sensor - 50kg [part_number=SEN-10245]
  part = ESP-WROOM-32 [ESP-32S] Module [part_number=ESP-WROOM-32]
  V1 = DC Power [voltage=5V]
  Pretending_1x3_Keypad = 1*4 Membrane Matrix Keypad

nets:
  N1: HX711.DO/RX, part.IO16
  N2: HX711.CK/TX, part.IO17
  N3: HX711.E+, S3.R
  N4: HX711.E-, S4.R
  N5: HX711.A+, S1.R
  N6: HX711.A-, S2.R
  N7: S1.B, S3.B
  N8: S1.W, S4.W
  N9: LoRa_Module1.NSS, part.IO5
  N10: LoRa_Module1.RESET, part.IO14
  N11: LoRa_Module1.DIO0, part.IO2
  N12: LCD1602_I2C.SDA, part.IO21
  N13: LCD1602_I2C.SCL, part.IO22
  N14: S2.B, S4.B
  N15: S2.W, S3.W
  N16: part.GND, V1.V-
  N17: part.IO25, Pretending_1x3_Keypad.pin4
  N18: part.IO4, Pretending_1x3_Keypad.pin1
  N19: part.IO18, Pretending_1x3_Keypad.pin2
  N20: part.IO19, Pretending_1x3_Keypad.pin3
  N21: part.RST, V1.V+

custom parts:
  Load Sensor - 50kg: Half-wheatstone bridge Load Cell modified from the Fritzing Repo This load sensor, sometimes called a strain gauge, is the same one found in digital bathroom scales (you know, the ones you use in January for your New Year's resolutions, and then forget about a month later). This sensor can measure up to about 110 pounds.
  Ra-01 - LoRa Module SX1278: The Ra-01 LoRa Module featuring the SX1278 engine by Semtech. Module by AI-Thinker. Module (Ra-01) specifications from: https://www.banggood.com/Ra-01-Smart-Electronics-SX1278-LoRa-Spread-Spectrum-Wireless-Module-Ultra-Far-10KM-433M-p-1130769.html Description: Power supply: DC1.8-3.7V(3.3V) Chip: SX1278 Frequency: 433Mhz Operating temperature: -40~+85°C On Sheild Description (may vary by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
  LCD1602-I2C: A standard character display, usually with 2x16 characters. Comes in many colors with LCM1602 IIC attached.
  ESP-WROOM-32 [ESP-32S] Module: Espressif ESP-WROOM-32 WiFi/Bluetooth LE microcontroller module also known as the Ai-Thinker ESP-32S module with similar formfactor. The ESP32 is a microcontroller chip with WiFi and BLE capabilities. The chip is developed by Espressif and is the successor to the popular ESP8266 WiFi module.
  1*4 Membrane Matrix Keypad: Membrane Matrix 1x4 Keypad
